# Fritzing sketch Diagrama de Conexion (saved by Fritzing 0.9.4)

parts:
  U1 = NodeMCU V1.0
  Componente1 = RFID-RC522-v2

nets:
  GND: U1.D1, U1.GND, U1.D5, U1.D6, U1.D7, Componente1.SCK, Componente1.MOSI, Componente1.MISO, Componente1.GND, Componente1.RST
  N1: U1.D2, Componente1.SDA
  3V3: U1.3V3, Componente1.3.3V

notes:
  Nodemcu | RC522
  D2 (4) SDA (verde)
  D5 SCK (Azul)
  D7 MOSI (Morado)
  D6 MISO (Gris)
  G (GND) GND (Negro)
  D1 (5) RST (Amarillo)
  3v3 3v3 (Rojo)

custom parts:
  NodeMCU V1.0: ESP8266 based NodeMCU V1.0
  RFID-RC522-v2: A simple China made RFID-RC522 Reader; do check the pin labels, as this is a MFRC522 based clone.
